// Logisim project Mux.circ as structural Verilog: 1 circuit, main circuit main
module main (
  input  in_1,
  input  in_2,
  input  in_3,
  input  [15:0] in_4,
  input  [15:0] in_5,
  input  in_6,
  output out_7,
  output [15:0] out_8
);

  wire and_1_out, and_2_out, not_1_out;
  wire [15:0] and_3_out, and_4_out, bit_extender_1_out, not_2_out;

  not not_1 (not_1_out, in_3);
  Bit_Extender #(.in_width(1), .\type ("input")) bit_extender_1 (.out(bit_extender_1_out), .extend(in_6));  // open: in
  assign not_2_out = ~bit_extender_1_out;  // NOT_Gate not_2, 16 bits wide
  and and_1 (and_1_out, in_1, not_1_out);
  and and_2 (and_2_out, in_2, in_3);
  assign and_3_out = in_4 & not_2_out;  // AND_Gate and_3, 16 bits wide
  assign and_4_out = in_5 & bit_extender_1_out;  // AND_Gate and_4, 16 bits wide
  or or_1 (out_7, and_1_out, and_2_out);
  assign out_8 = and_3_out | and_4_out;  // OR_Gate or_2, 16 bits wide
endmodule
