// Logisim project Basic.circ as structural Verilog: 1 circuit, main circuit main
module main (
  input  a,
  input  a_2,
  input  b,
  input  a_3,
  input  b_2,
  input  a_4,
  input  b_3,
  output out,
  output out_2,
  output out_3,
  output out_4
);

  wire nand_1_out, nand_3_out, nand_4_out, nand_5_out, nand_8_out, nand_9_out;

  nand nand_1 (nand_1_out, a_2, b);
  nand nand_2 (out, a, a);
  nand nand_3 (nand_3_out, a_3, a_3);
  nand nand_4 (nand_4_out, b_2, b_2);
  nand nand_5 (nand_5_out, a_4, b_3);
  nand nand_6 (out_2, nand_1_out, nand_1_out);
  nand nand_7 (out_3, nand_3_out, nand_4_out);
  nand nand_8 (nand_8_out, a_4, nand_5_out);
  nand nand_9 (nand_9_out, nand_5_out, b_3);
  nand nand_10 (out_4, nand_8_out, nand_9_out);
endmodule
