// Logisim project Basic16.circ as structural Verilog: 1 circuit, main circuit main
module main (
  input  [15:0] a,
  input  [15:0] a_2,
  input  [15:0] b,
  input  [15:0] a_3,
  input  [15:0] b_2,
  input  [15:0] a_4,
  input  [15:0] b_3,
  output [15:0] out,
  output [15:0] out_2,
  output [15:0] out_3,
  output [15:0] out_4
);

  wire [15:0] nand_1_out, nand_3_out, nand_4_out, nand_5_out, nand_8_out, nand_9_out;

  assign nand_1_out = ~(a_2 & b);  // NAND_Gate nand_1, 16 bits wide
  assign out = ~(a & a);  // NAND_Gate nand_2, 16 bits wide
  assign nand_3_out = ~(a_3 & a_3);  // NAND_Gate nand_3, 16 bits wide
  assign nand_4_out = ~(b_2 & b_2);  // NAND_Gate nand_4, 16 bits wide
  assign nand_5_out = ~(a_4 & b_3);  // NAND_Gate nand_5, 16 bits wide
  assign out_2 = ~(nand_1_out & nand_1_out);  // NAND_Gate nand_6, 16 bits wide
  assign out_3 = ~(nand_3_out & nand_4_out);  // NAND_Gate nand_7, 16 bits wide
  assign nand_8_out = ~(a_4 & nand_5_out);  // NAND_Gate nand_8, 16 bits wide
  assign nand_9_out = ~(nand_5_out & b_3);  // NAND_Gate nand_9, 16 bits wide
  assign out_4 = ~(nand_8_out & nand_9_out);  // NAND_Gate nand_10, 16 bits wide
endmodule
