// Logisim project DMux.circ as structural Verilog: 1 circuit, main circuit main
module main (
  input  in,
  input  sel,
  input  [15:0] in_2,
  input  sel_2,
  output a,
  output b,
  output [15:0] a_2,
  output [15:0] b_2
);

  wire not_1_out;
  wire [15:0] bit_extender_1_out, not_2_out;

  not not_1 (not_1_out, sel);
  Bit_Extender #(.in_width(1), .\type ("input")) bit_extender_1 (.out(bit_extender_1_out), .extend(sel_2));  // open: in
  and and_1 (a, in, not_1_out);
  and and_2 (b, in, sel);
  assign not_2_out = ~bit_extender_1_out;  // NOT_Gate not_2, 16 bits wide
  assign a_2 = in_2 & not_2_out;  // AND_Gate and_3, 16 bits wide
  assign b_2 = in_2 & bit_extender_1_out;  // AND_Gate and_4, 16 bits wide
endmodule
