// Logisim project DMux8Way.circ as structural Verilog: 1 circuit, main circuit main
module main (
  input  in,
  input  [2:0] sel,
  output a,
  output b,
  output c,
  output d,
  output e,
  output f,
  output g,
  output h
);

  wire demultiplexer_1_out0, demultiplexer_1_out1;

  Demultiplexer #(.enable("false")) demultiplexer_1 (
    .out0(demultiplexer_1_out0), .out1(demultiplexer_1_out1), .in(in), .sel(sel[2]));
  Demultiplexer #(.enable("false"), .select(2)) demultiplexer_2 (
    .out0(a), .out1(b), .out2(c), .out3(d), .in(demultiplexer_1_out0), .sel(sel[1:0]));
  Demultiplexer #(.enable("false"), .select(2)) demultiplexer_3 (
    .out0(e), .out1(f), .out2(g), .out3(h), .in(demultiplexer_1_out1), .sel(sel[1:0]));
endmodule
