// Logisim project HalfFullAdder.circ as structural Verilog: 1 circuit, main circuit main
module main (
  input  a,
  input  b,
  input  a_2,
  input  b_2,
  input  c_in,
  output sum,
  output carry,
  output sum_2,
  output c_out
);

  wire and_2_out, and_3_out, xor_2_out;

  xor xor_1 (sum, a, b);
  and and_1 (carry, a, b);
  xor xor_2 (xor_2_out, a_2, b_2);
  xor xor_3 (sum_2, xor_2_out, c_in);
  and and_2 (and_2_out, xor_2_out, c_in);
  and and_3 (and_3_out, b_2, a_2);
  or or_1 (c_out, and_2_out, and_3_out);
endmodule
