// Logisim project Inc16.circ as structural Verilog: 1 circuit, main circuit main
module main (
  input  [5:0] in,
  output [5:0] out
);

  Adder #(.width(6)) adder_1 (.a(in), .b(6'b000001), .out(out));  // open: cin, cout
endmodule
