// Logisim project Mux4Way16.circ as structural Verilog: 1 circuit, main circuit main
module main (
  input  [15:0] a,
  input  [15:0] b,
  input  [15:0] c,
  input  [15:0] d,
  input  [1:0] sel,
  output [15:0] out
);

  wire [15:0] multiplexer_1_out, multiplexer_2_out;

  Multiplexer #(.enable("false"), .width(16)) multiplexer_1 (.in0(a), .in1(b), .out(multiplexer_1_out), .sel(sel[0]));
  Multiplexer #(.enable("false"), .width(16)) multiplexer_2 (.in0(c), .in1(d), .out(multiplexer_2_out), .sel(sel[0]));
  Multiplexer #(.enable("false"), .width(16)) multiplexer_3 (
    .in0(multiplexer_1_out), .in1(multiplexer_2_out), .out(out), .sel(sel[1]));
endmodule
