// Logisim project Mux8Way16.circ as structural Verilog: 1 circuit, main circuit main
module main (
  input  [15:0] a,
  input  [15:0] b,
  input  [15:0] c,
  input  [15:0] d,
  input  [15:0] e,
  input  [15:0] f,
  input  [15:0] g,
  input  [15:0] h,
  input  [2:0] sel,
  output [15:0] out
);

  wire [15:0] multiplexer_1_out, multiplexer_2_out;

  Multiplexer #(.enable("false"), .select(2), .width(16)) multiplexer_1 (
    .in0(a), .in1(b), .in2(c), .in3(d), .out(multiplexer_1_out), .sel(sel[1:0]));
  Multiplexer #(.enable("false"), .select(2), .width(16)) multiplexer_2 (
    .in0(e), .in1(f), .in2(g), .in3(h), .out(multiplexer_2_out), .sel(sel[1:0]));
  Multiplexer #(.enable("false"), .width(16)) multiplexer_3 (
    .in0(multiplexer_1_out), .in1(multiplexer_2_out), .out(out), .sel(sel[2]));
endmodule
