// Logisim project PC.circ as structural Verilog: 1 circuit, main circuit main
module main (
  input  inc,
  input  load,
  input  reset,
  input  [15:0] in,
  output [15:0] out
);

  wire clock_out;
  wire [15:0] adder_1_out, multiplexer_1_out, multiplexer_2_out, multiplexer_3_out;

  Clock clock (.out(clock_out));
  Register #(.width(16)) register_1 (.D(multiplexer_3_out), .Q(out), .clk(clock_out));  // open: en, clr
  Adder #(.width(16)) adder_1 (.a(out), .b(16'h1), .out(adder_1_out));  // open: cin, cout
  Multiplexer #(.enable("false"), .width(16)) multiplexer_1 (
    .in0(out), .in1(adder_1_out), .out(multiplexer_1_out), .sel(inc));
  Multiplexer #(.enable("false"), .width(16)) multiplexer_2 (
    .in0(multiplexer_1_out), .in1(in), .out(multiplexer_2_out), .sel(load));
  Multiplexer #(.enable("false"), .width(16)) multiplexer_3 (
    .in0(multiplexer_2_out), .in1({16{1'b0}}), .out(multiplexer_3_out), .sel(reset));
endmodule
