// Logisim project CPU.circ as structural Verilog: 5 circuits, main circuit main
module Jumper (
  input  zr,
  input  ng,
  input  [2:0] opcode,
  output out
);

  wire and_1_out, not_1_out, not_2_out, or_1_out;

  not not_1 (not_1_out, zr);
  not not_2 (not_2_out, ng);
  and and_1 (and_1_out, not_1_out, not_2_out);
  or or_1 (or_1_out, zr, ng);
  Multiplexer #(.enable("false"), .select(3)) multiplexer_1 (
    .in0(1'b0), .in1(and_1_out), .in2(zr), .in3(not_2_out), .in4(ng), .in5(not_1_out), .in6(or_1_out),
    .in7(1'b1), .out(out), .sel(opcode));
endmodule

module PC (
  input  inc,
  input  load,
  input  reset,
  input  [15:0] in,
  input  clk,
  output [15:0] out
);

  wire [15:0] adder_1_out, multiplexer_1_out, multiplexer_2_out, multiplexer_3_out;

  Register #(.width(16)) register_1 (.D(multiplexer_3_out), .Q(out), .clk(clk));  // open: en, clr
  Adder #(.width(16)) adder_1 (.a(out), .b(16'h1), .out(adder_1_out));  // open: cin, cout
  Multiplexer #(.enable("false"), .width(16)) multiplexer_1 (
    .in0(out), .in1(adder_1_out), .out(multiplexer_1_out), .sel(inc));
  Multiplexer #(.enable("false"), .width(16)) multiplexer_2 (
    .in0(multiplexer_1_out), .in1(in), .out(multiplexer_2_out), .sel(load));
  Multiplexer #(.enable("false"), .width(16)) multiplexer_3 (
    .in0(multiplexer_2_out), .in1({16{1'b0}}), .out(multiplexer_3_out), .sel(reset));
endmodule

module ALU (
  input  [15:0] x,
  input  zx,
  input  nx,
  input  [15:0] y,
  input  f,
  input  nout,
  input  zy,
  input  ny,
  output zr,
  output ng,
  output [15:0] out
);

  wire [15:0] adder_1_out, and_1_out, multiplexer_1_out, multiplexer_2_out, multiplexer_3_out,
       multiplexer_4_out, multiplexer_5_out, not_1_out, not_2_out, not_3_out;

  Multiplexer #(.enable("false"), .width(16)) multiplexer_1 (
    .in0(x), .in1({16{1'b0}}), .out(multiplexer_1_out), .sel(zx));
  Multiplexer #(.enable("false"), .width(16)) multiplexer_2 (
    .in0(y), .in1({16{1'b0}}), .out(multiplexer_2_out), .sel(zy));
  Multiplexer #(.enable("false"), .width(16)) multiplexer_3 (
    .in0(multiplexer_1_out), .in1(not_1_out), .out(multiplexer_3_out), .sel(nx));
  assign not_1_out = ~multiplexer_1_out;  // NOT_Gate not_1, 16 bits wide
  Multiplexer #(.enable("false"), .width(16)) multiplexer_4 (
    .in0(multiplexer_2_out), .in1(not_2_out), .out(multiplexer_4_out), .sel(ny));
  assign not_2_out = ~multiplexer_2_out;  // NOT_Gate not_2, 16 bits wide
  assign and_1_out = multiplexer_3_out & multiplexer_4_out;  // AND_Gate and_1, 16 bits wide
  Adder #(.width(16)) adder_1 (
    .a(multiplexer_3_out), .b(multiplexer_4_out), .out(adder_1_out), .cin(1'b0));  // open: cout
  Multiplexer #(.enable("false"), .width(16)) multiplexer_5 (
    .in0(and_1_out), .in1(adder_1_out), .out(multiplexer_5_out), .sel(f));
  assign not_3_out = ~multiplexer_5_out;  // NOT_Gate not_3, 16 bits wide
  Multiplexer #(.enable("false"), .width(16)) multiplexer_6 (
    .in0(multiplexer_5_out), .in1(not_3_out), .out({ng, out[14:0]}), .sel(nout));
  nor nor_1 (zr, out[0], out[1], out[2], out[3], out[4], out[5], out[6], out[7], out[8], out[9], out[10], out[11], out[12], out[13], out[14], ng);

  assign out[15] = ng;
endmodule

module Loader (
  input  d1,
  input  d2,
  input  d3,
  input  ctype,
  output loadA,
  output loadD,
  output loadM
);

  and and_1 (loadA, d1, ctype);
  and and_2 (loadD, d2, ctype);
  and and_3 (loadM, d3, ctype);
endmodule

module main (
  input  [15:0] inM,
  input  [15:0] instruction,
  input  reset,
  output [15:0] outM,
  output [14:0] addressM,
  output [14:0] pc,
  output writeM
);

  wire alu_1_ng, alu_1_zr, clk_out, jumper_1_out, Loader_loada, Loader_loadd, not_1_out, or_1_out;
  wire [15:0] D_Register_q, multiplexer_1_out, multiplexer_2_out;
  wire [15:15] A_Register_q, pc_1_out;

  Clock clk (.out(clk_out));
  not not_1 (not_1_out, instruction[15]);
  Loader Loader (
    .d1(instruction[5]), .d2(instruction[4]), .d3(instruction[3]), .ctype(instruction[15]),
    .loadA(Loader_loada), .loadD(Loader_loadd), .loadM(writeM));
  or or_1 (or_1_out, not_1_out, Loader_loada);
  Multiplexer #(.enable("false"), .width(16)) multiplexer_1 (
    .in0(outM), .in1(instruction), .out(multiplexer_1_out), .sel(not_1_out));
  Register #(.width(16)) D_Register (.D(outM), .en(Loader_loadd), .Q(D_Register_q), .clk(clk_out));  // open: clr
  Register #(.width(16)) A_Register (
    .D(multiplexer_1_out), .en(or_1_out), .Q({A_Register_q[15], addressM}), .clk(clk_out));  // open: clr
  Multiplexer #(.enable("false"), .width(16)) multiplexer_2 (
    .in0({A_Register_q[15], addressM}), .in1(inM), .out(multiplexer_2_out), .sel(instruction[12]));
  ALU alu_1 (
    .x(D_Register_q), .y(multiplexer_2_out), .zr(alu_1_zr), .ng(alu_1_ng), .out(outM), .zx(instruction[11]),
    .zy(instruction[9]), .nx(instruction[10]), .ny(instruction[8]), .f(instruction[7]), .nout(instruction[6]));
  Jumper jumper_1 (.zr(alu_1_zr), .ng(alu_1_ng), .opcode(instruction[2:0]), .out(jumper_1_out));
  PC pc_1 (
    .out({pc_1_out[15], pc}), .inc(1'b1), .load(jumper_1_out), .reset(reset),
    .in({A_Register_q[15], addressM}), .clk(clk_out));

  // Notes on the sheet:
  //   isAinstruction
endmodule
