// Logisim project Jumper.circ as structural Verilog: 1 circuit, main circuit main
module main (
  input  zr,
  input  ng,
  input  [2:0] opcode,
  output out
);

  wire and_1_out, not_1_out, not_2_out, or_1_out;

  not not_1 (not_1_out, zr);
  not not_2 (not_2_out, ng);
  and and_1 (and_1_out, not_1_out, not_2_out);
  or or_1 (or_1_out, zr, ng);
  Multiplexer #(.enable("false"), .select(3)) multiplexer_1 (
    .in0(1'b0), .in1(and_1_out), .in2(zr), .in3(not_2_out), .in4(ng), .in5(not_1_out), .in6(or_1_out),
    .in7(1'b1), .out(out), .sel(opcode));
endmodule
