// Logisim project Loader.circ as structural Verilog: 1 circuit, main circuit main
module main (
  input  d1,
  input  d2,
  input  d3,
  input  ctype,
  output loadA,
  output loadD,
  output loadM
);

  and and_1 (loadA, d1, ctype);
  and and_2 (loadD, d2, ctype);
  and and_3 (loadM, d3, ctype);
endmodule
